// Logisim project lab8.circ as structural Verilog: 2 circuits, main circuit ParityGenerator
module XOR (
  input  X,
  input  Y,
  output out_3
);


  // Notes on the sheet:
  //   Use minterm expansion to create an XOR gate using AND + OR gates
endmodule

module ParityGenerator (
  input  X,
  input  Y,
  input  Z,
  input  x_2,
  input  y_2,
  output Parity
);

  wire and_1_out, and_2_out, and_3_out, and_4_out, not_1_out, not_2_out, or_1_out, or_2_out, xor_1_out,
       xor_2_out;

  and and_1 (and_1_out, X, Y);
  and and_2 (and_2_out, and_1_out, Z);
  xor xor_1 (xor_1_out, X, Y);
  xor xor_2 (xor_2_out, Z, xor_1_out);
  or or_1 (or_1_out, and_2_out, xor_2_out);
  not not_1 (not_1_out, x_2);
  not not_2 (not_2_out, y_2);
  // XOR_Gate xor_3 is placed but not wired
  and and_3 (and_3_out, not_1_out, y_2);
  and and_4 (and_4_out, x_2, not_2_out);
  or or_2 (or_2_out, and_3_out, and_4_out);

  // Notes on the sheet:
  //   Input Bits
  //   XOR, denoted by:
  //   is equivalent to:
  //   Output Bit
  //   Write your parity circuit here
  //   the output = 1 if an odd number of inputs (1 or 3) are 1, otherwise 0
  //   ONLY use: NOT, AND, OR, and any custom functions you write (included in the .circ submission)
  //   WRITE YOUR NAME AND PLEDGE SOMEWHERE IN THIS CIRCUIT
  //   I pledge my honoI that I have abided by the Stevens Honor System. - Jason Qiu
endmodule
